# Fritzing sketch Weevle_Soldering (saved by Fritzing 0.9.6b)
breadboards: 1

parts:
  R1 = PHOTOCELL [package=photocell-kit]
  BAT1 = Battery Holders [package=battcom_20mm_pth]
  R2 = Resistor [tolerance=±5% power=0.25 resistance=47k package=THT]
  R3 = Resistor [tolerance=±5% resistance=220 package="0402 [SMD]"]
  R4 = Resistor [tolerance=±5% resistance=220 package="0402 [SMD]"]
  LED2 = smd LED [color="Red (633nm)" package="0805 [SMD]"]
  Q1 = NPN-Transistor [package="SOT-23 [SMD]"]
  LED1 = smd LED [color="Red (633nm)" package="0805 [SMD]"]

nets:
  N1: R1.P$1, Q1.0
  N2: R1.P$2, BAT1.+, R2.Pin_1
  N3: BAT1.-, LED2.cathode, LED1.cathode
  N4: R2.Pin_0, Q1.1
  N5: R3.Pin_0, LED1.anode
  N6: R3.Pin_1, R4.Pin_0, Q1.2
  N7: R4.Pin_1, LED2.anode
